// Logisim project uklad_d.circ as structural Verilog: 1 circuit, main circuit main
module main (
  input  X,
  input  CLK
);

  wire n7400_1_pin2, n7400_1_pin3, n7400_1_pin8, n7400_1_pin11, n7400_1_pin12, n7400_1_pin13, n7402_1_pin1,
       n7402_1_pin3, n7402_1_pin12, n7402_1_pin13, n7474_1_pin1;

  _7400 u_7400_1 (
    .pin1(X), .pin2(n7400_1_pin2), .pin3(n7400_1_pin3), .pin13(n7400_1_pin13), .pin12(n7400_1_pin12),
    .pin11(n7400_1_pin11), .pin10(n7400_1_pin11), .pin9(n7400_1_pin3), .pin8(n7400_1_pin8));  // open: pin4, pin5, pin6
  _7404 u_7404_1 (
    .pin13(X), .pin12(n7400_1_pin13));  // open: pin1, pin2, pin3, pin4, pin5, pin6, pin11, pin10, pin9, pin8
  LED Z2 (.in(n7402_1_pin13));
  _7402 u_7402_1 (
    .pin1(n7402_1_pin1), .pin2(n7400_1_pin2), .pin3(n7402_1_pin3), .pin13(n7402_1_pin13),
    .pin12(n7402_1_pin12), .pin11(n7400_1_pin12));  // open: pin4, pin5, pin6, pin10, pin9, pin8
  LED Z1 (.in(n7402_1_pin1));
  _7474 u_7474_1 (
    .pin1(n7474_1_pin1), .pin2(n7400_1_pin8), .pin3(CLK), .pin4(n7474_1_pin1), .pin5(n7400_1_pin12),
    .pin6(n7400_1_pin2), .pin13(n7474_1_pin1), .pin12(n7400_1_pin12), .pin11(CLK), .pin10(n7474_1_pin1),
    .pin9(n7402_1_pin3), .pin8(n7402_1_pin12));
  // also tied to VCC on the sheet: n7474_1_pin1
endmodule
