// Logisim project uklad_jk.circ as structural Verilog: 1 circuit, main circuit main
module main (
  input  X,
  input  CLK
);

  wire j_k_ff_1_q, j_k_ff_1_qn, n7402_1_pin10, n7402_1_pin13, n7404_1_pin8;

  _7404 u_7404_1 (
    .pin9(X), .pin8(n7404_1_pin8));  // open: pin1, pin2, pin3, pin4, pin5, pin6, pin13, pin12, pin11, pin10
  J_K_Flip_Flop j_k_ff_1 (.J(X), .K(X), .clk(CLK), .Q(j_k_ff_1_q), .Qn(j_k_ff_1_qn));  // open: preset, reset
  _7402 u_7402_1 (
    .pin13(n7402_1_pin13), .pin12(n7404_1_pin8), .pin11(j_k_ff_1_qn), .pin10(n7402_1_pin10),
    .pin9(n7404_1_pin8), .pin8(j_k_ff_1_q));  // open: pin1, pin2, pin3, pin4, pin5, pin6
  LED Z1 (.in(n7402_1_pin13));
  LED Z2 (.in(n7402_1_pin10));
endmodule
